// Logisim project datapath.circ as structural Verilog
module ULA (
  input  [3:0] Operador,
  input  [4:0] SHAMT,
  input  [31:0] A,
  input  [31:0] B,
  output [31:0] Resultado,
  output out_6,
  output Overflow
);

  wire and_2_out, and_3_out, and_4_out, and_5_out, comparator_2_eq, comparator_3_eq, not_1_out, not_2_out,
       not_3_out, not_4_out, not_5_out, not_6_out;
  wire [31:0] adder_1_out, and_1_out, comparator_1_lt, nor_1_out, or_1_out, shifter_1_out, shifter_2_out,
       subtractor_1_out, xor_1_out;

  assign and_1_out = A & B;  // AND_Gate and_1, 32 bits wide
  assign or_1_out = A | B;  // OR_Gate or_1, 32 bits wide
  assign nor_1_out = ~(A | B);  // NOR_Gate nor_1, 32 bits wide
  assign xor_1_out = A ^ B;  // XOR_Gate xor_1, 32 bits wide
  Adder #(.width(32)) adder_1 (.a(A), .b(B), .out(adder_1_out));  // open: cin, cout
  Subtractor #(.width(32)) subtractor_1 (.a(A), .b(B), .out(subtractor_1_out));  // open: bin, bout
  Shifter #(.width(32)) shifter_1 (.in(A), .\dist (SHAMT), .out(shifter_1_out));
  Shifter #(.width(32), .shift("lr")) shifter_2 (.in(A), .\dist (SHAMT), .out(shifter_2_out));
  Comparator #(.width(32)) comparator_1 (.a(A), .b(B), .lt(comparator_1_lt[0]));  // open: gt, eq
  Multiplexer #(.select(4), .width(32), .enable("false")) multiplexer_1 (
    .in0(and_1_out), .in1(or_1_out), .in2(nor_1_out), .in3(xor_1_out), .in4(adder_1_out),
    .in5(subtractor_1_out), .in6(shifter_1_out), .in7(shifter_2_out), .in8(comparator_1_lt), .out(Resultado),
    .sel(Operador));  // open: in9, in10, in11, in12, in13, in14, in15
  Comparator #(.width(4)) comparator_2 (.a(Operador), .b(4'b0100), .eq(comparator_2_eq));  // open: gt, lt
  Comparator #(.width(4)) comparator_3 (.a(Operador), .b(4'b0101), .eq(comparator_3_eq));  // open: gt, lt
  not not_1 (not_1_out, Resultado[31]);
  not not_2 (not_2_out, B[31]);
  not not_3 (not_3_out, A[31]);
  not not_4 (not_4_out, A[31]);
  not not_5 (not_5_out, Resultado[31]);
  not not_6 (not_6_out, B[31]);
  and and_2 (and_2_out, not_1_out, comparator_2_eq, B[31], A[31]);
  and and_3 (and_3_out, Resultado[31], comparator_2_eq, not_2_out, not_3_out);
  and and_4 (and_4_out, Resultado[31], comparator_3_eq, B[31], not_4_out);
  and and_5 (and_5_out, not_5_out, comparator_3_eq, not_6_out, A[31]);
  Comparator #(.width(32)) comparator_4 (.a(Resultado), .b({32{1'b0}}), .eq(out_6));  // open: gt, lt
  or or_2 (Overflow, and_2_out, and_3_out, and_4_out, and_5_out);

  // Notes on the sheet:
  //   Shift Amount
  //   negativo + negativo = positivo
  //   positivo + positivo = negativo
  //   positivo - negativo = negativo
  //   negativo - positivo = positivo
  //   ZERO
endmodule

module Registradores (
  input  [4:0] LR1,
  input  [4:0] LR2,
  input  [31:0] WD,
  input  [4:0] WR,
  input  RW,
  output [31:0] LD1,
  output [31:0] LD2
);

  wire clock_1_out, demultiplexer_2_out0, demultiplexer_2_out1, demultiplexer_2_out2, demultiplexer_2_out3,
       demultiplexer_2_out4, demultiplexer_2_out5, demultiplexer_2_out6, demultiplexer_2_out7,
       demultiplexer_2_out8, demultiplexer_2_out9, demultiplexer_2_out10, demultiplexer_2_out11,
       demultiplexer_2_out12, demultiplexer_2_out13, demultiplexer_2_out14, demultiplexer_2_out15,
       demultiplexer_2_out16, demultiplexer_2_out17, demultiplexer_2_out18, demultiplexer_2_out19,
       demultiplexer_2_out20, demultiplexer_2_out21, demultiplexer_2_out22, demultiplexer_2_out23,
       demultiplexer_2_out24, demultiplexer_2_out25, demultiplexer_2_out26, demultiplexer_2_out27,
       demultiplexer_2_out28, demultiplexer_2_out29, demultiplexer_2_out30, demultiplexer_2_out31;
  wire [31:0] demultiplexer_1_out0, demultiplexer_1_out1, demultiplexer_1_out2, demultiplexer_1_out3,
       demultiplexer_1_out4, demultiplexer_1_out5, demultiplexer_1_out6, demultiplexer_1_out7,
       demultiplexer_1_out8, demultiplexer_1_out9, demultiplexer_1_out10, demultiplexer_1_out11,
       demultiplexer_1_out12, demultiplexer_1_out13, demultiplexer_1_out14, demultiplexer_1_out15,
       demultiplexer_1_out16, demultiplexer_1_out17, demultiplexer_1_out18, demultiplexer_1_out19,
       demultiplexer_1_out20, demultiplexer_1_out21, demultiplexer_1_out22, demultiplexer_1_out23,
       demultiplexer_1_out24, demultiplexer_1_out25, demultiplexer_1_out26, demultiplexer_1_out27,
       demultiplexer_1_out28, demultiplexer_1_out29, demultiplexer_1_out30, demultiplexer_1_out31, s0_q,
       s1_q, s2_q, s3_q, s4_q, s5_q, s6_q, s7_q, s8_q, s9_q, s10_q, s11_q, s12_q, s13_q, s14_q, s15_q, s16_q,
       s17_q, s18_q, s19_q, s20_q, s21_q, s22_q, s23_q, s24_q, s25_q, s26_q, s27_q, s28_q, s29_q, s30_q,
       s31_q;

  Clock clock_1 (.out(clock_1_out));
  Demultiplexer #(.select(5), .width(32), .enable("false")) demultiplexer_1 (
    .out0(demultiplexer_1_out0), .out1(demultiplexer_1_out1), .out2(demultiplexer_1_out2),
    .out3(demultiplexer_1_out3), .out4(demultiplexer_1_out4), .out5(demultiplexer_1_out5),
    .out6(demultiplexer_1_out6), .out7(demultiplexer_1_out7), .out8(demultiplexer_1_out8),
    .out9(demultiplexer_1_out9), .out10(demultiplexer_1_out10), .out11(demultiplexer_1_out11),
    .out12(demultiplexer_1_out12), .out13(demultiplexer_1_out13), .out14(demultiplexer_1_out14),
    .out15(demultiplexer_1_out15), .out16(demultiplexer_1_out16), .out17(demultiplexer_1_out17),
    .out18(demultiplexer_1_out18), .out19(demultiplexer_1_out19), .out20(demultiplexer_1_out20),
    .out21(demultiplexer_1_out21), .out22(demultiplexer_1_out22), .out23(demultiplexer_1_out23),
    .out24(demultiplexer_1_out24), .out25(demultiplexer_1_out25), .out26(demultiplexer_1_out26),
    .out27(demultiplexer_1_out27), .out28(demultiplexer_1_out28), .out29(demultiplexer_1_out29),
    .out30(demultiplexer_1_out30), .out31(demultiplexer_1_out31), .in(WD), .sel(WR));
  Demultiplexer #(.select(5), .enable("false")) demultiplexer_2 (
    .out0(demultiplexer_2_out0), .out1(demultiplexer_2_out1), .out2(demultiplexer_2_out2),
    .out3(demultiplexer_2_out3), .out4(demultiplexer_2_out4), .out5(demultiplexer_2_out5),
    .out6(demultiplexer_2_out6), .out7(demultiplexer_2_out7), .out8(demultiplexer_2_out8),
    .out9(demultiplexer_2_out9), .out10(demultiplexer_2_out10), .out11(demultiplexer_2_out11),
    .out12(demultiplexer_2_out12), .out13(demultiplexer_2_out13), .out14(demultiplexer_2_out14),
    .out15(demultiplexer_2_out15), .out16(demultiplexer_2_out16), .out17(demultiplexer_2_out17),
    .out18(demultiplexer_2_out18), .out19(demultiplexer_2_out19), .out20(demultiplexer_2_out20),
    .out21(demultiplexer_2_out21), .out22(demultiplexer_2_out22), .out23(demultiplexer_2_out23),
    .out24(demultiplexer_2_out24), .out25(demultiplexer_2_out25), .out26(demultiplexer_2_out26),
    .out27(demultiplexer_2_out27), .out28(demultiplexer_2_out28), .out29(demultiplexer_2_out29),
    .out30(demultiplexer_2_out30), .out31(demultiplexer_2_out31), .in(RW), .sel(WR));
  Register #(.width(32)) s0 (
    .D(demultiplexer_1_out0), .en(demultiplexer_2_out0), .Q(s0_q), .clk(clock_1_out));  // open: clr
  Register #(.width(32)) s1 (
    .D(demultiplexer_1_out1), .en(demultiplexer_2_out1), .Q(s1_q), .clk(clock_1_out));  // open: clr
  Register #(.width(32)) s2 (
    .D(demultiplexer_1_out2), .en(demultiplexer_2_out2), .Q(s2_q), .clk(clock_1_out));  // open: clr
  Register #(.width(32)) s3 (
    .D(demultiplexer_1_out3), .en(demultiplexer_2_out3), .Q(s3_q), .clk(clock_1_out));  // open: clr
  Register #(.width(32)) s4 (
    .D(demultiplexer_1_out4), .en(demultiplexer_2_out4), .Q(s4_q), .clk(clock_1_out));  // open: clr
  Register #(.width(32)) s5 (
    .D(demultiplexer_1_out5), .en(demultiplexer_2_out5), .Q(s5_q), .clk(clock_1_out));  // open: clr
  Register #(.width(32)) s6 (
    .D(demultiplexer_1_out6), .en(demultiplexer_2_out6), .Q(s6_q), .clk(clock_1_out));  // open: clr
  Register #(.width(32)) s7 (
    .D(demultiplexer_1_out7), .en(demultiplexer_2_out7), .Q(s7_q), .clk(clock_1_out));  // open: clr
  Register #(.width(32)) s8 (
    .D(demultiplexer_1_out8), .en(demultiplexer_2_out8), .Q(s8_q), .clk(clock_1_out));  // open: clr
  Register #(.width(32)) s9 (
    .D(demultiplexer_1_out9), .en(demultiplexer_2_out9), .Q(s9_q), .clk(clock_1_out));  // open: clr
  Register #(.width(32)) s10 (
    .D(demultiplexer_1_out10), .en(demultiplexer_2_out10), .Q(s10_q), .clk(clock_1_out));  // open: clr
  Register #(.width(32)) s11 (.D(demultiplexer_1_out11), .en(demultiplexer_2_out11), .Q(s11_q));  // open: clk, clr
  Register #(.width(32)) s12 (
    .D(demultiplexer_1_out12), .en(demultiplexer_2_out12), .Q(s12_q), .clk(clock_1_out));  // open: clr
  Register #(.width(32)) s13 (
    .D(demultiplexer_1_out13), .en(demultiplexer_2_out13), .Q(s13_q), .clk(clock_1_out));  // open: clr
  Register #(.width(32)) s14 (
    .D(demultiplexer_1_out14), .en(demultiplexer_2_out14), .Q(s14_q), .clk(clock_1_out));  // open: clr
  Register #(.width(32)) s15 (
    .D(demultiplexer_1_out15), .en(demultiplexer_2_out15), .Q(s15_q), .clk(clock_1_out));  // open: clr
  Register #(.width(32)) s16 (
    .D(demultiplexer_1_out16), .en(demultiplexer_2_out16), .Q(s16_q), .clk(clock_1_out));  // open: clr
  Register #(.width(32)) s17 (
    .D(demultiplexer_1_out17), .en(demultiplexer_2_out17), .Q(s17_q), .clk(clock_1_out));  // open: clr
  Register #(.width(32)) s18 (
    .D(demultiplexer_1_out18), .en(demultiplexer_2_out18), .Q(s18_q), .clk(clock_1_out));  // open: clr
  Register #(.width(32)) s19 (
    .D(demultiplexer_1_out19), .en(demultiplexer_2_out19), .Q(s19_q), .clk(clock_1_out));  // open: clr
  Register #(.width(32)) s20 (
    .D(demultiplexer_1_out20), .en(demultiplexer_2_out20), .Q(s20_q), .clk(clock_1_out));  // open: clr
  Register #(.width(32)) s21 (
    .D(demultiplexer_1_out21), .en(demultiplexer_2_out21), .Q(s21_q), .clk(clock_1_out));  // open: clr
  Register #(.width(32)) s22 (
    .D(demultiplexer_1_out22), .en(demultiplexer_2_out22), .Q(s22_q), .clk(clock_1_out));  // open: clr
  Register #(.width(32)) s23 (
    .D(demultiplexer_1_out23), .en(demultiplexer_2_out23), .Q(s23_q), .clk(clock_1_out));  // open: clr
  Register #(.width(32)) s24 (
    .D(demultiplexer_1_out24), .en(demultiplexer_2_out24), .Q(s24_q), .clk(clock_1_out));  // open: clr
  Register #(.width(32)) s25 (
    .D(demultiplexer_1_out25), .en(demultiplexer_2_out25), .Q(s25_q), .clk(clock_1_out));  // open: clr
  Register #(.width(32)) s26 (
    .D(demultiplexer_1_out26), .en(demultiplexer_2_out26), .Q(s26_q), .clk(clock_1_out));  // open: clr
  Register #(.width(32)) s27 (.D(demultiplexer_1_out27), .en(demultiplexer_2_out27), .Q(s27_q));  // open: clk, clr
  Register #(.width(32)) s28 (
    .D(demultiplexer_1_out28), .en(demultiplexer_2_out28), .Q(s28_q), .clk(clock_1_out));  // open: clr
  Register #(.width(32)) s29 (
    .D(demultiplexer_1_out29), .en(demultiplexer_2_out29), .Q(s29_q), .clk(clock_1_out));  // open: clr
  Register #(.width(32)) s30 (
    .D(demultiplexer_1_out30), .en(demultiplexer_2_out30), .Q(s30_q), .clk(clock_1_out));  // open: clr
  Register #(.width(32)) s31 (
    .D(demultiplexer_1_out31), .en(demultiplexer_2_out31), .Q(s31_q), .clk(clock_1_out));  // open: clr
  Multiplexer #(.select(5), .width(32), .enable("false")) multiplexer_1 (
    .in0(s0_q), .in1(s1_q), .in2(s2_q), .in3(s3_q), .in4(s4_q), .in5(s5_q), .in6(s6_q), .in7(s7_q),
    .in8(s8_q), .in9(s9_q), .in10(s10_q), .in11(s11_q), .in12(s12_q), .in13(s13_q), .in14(s14_q),
    .in15(s15_q), .in16(s16_q), .in17(s17_q), .in18(s18_q), .in19(s19_q), .in20(s20_q), .in21(s21_q),
    .in22(s22_q), .in23(s23_q), .in24(s24_q), .in25(s25_q), .in26(s26_q), .in27(s27_q), .in28(s28_q),
    .in29(s29_q), .in30(s30_q), .in31(s31_q), .out(LD1), .sel(LR1));
  Multiplexer #(.select(5), .width(32), .enable("false")) multiplexer_2 (
    .in0(s0_q), .in1(s1_q), .in2(s2_q), .in3(s3_q), .in4(s4_q), .in5(s5_q), .in6(s6_q), .in7(s7_q),
    .in8(s8_q), .in9(s9_q), .in10(s10_q), .in11(s11_q), .in12(s12_q), .in13(s13_q), .in14(s14_q),
    .in15(s15_q), .in16(s16_q), .in17(s17_q), .in18(s18_q), .in19(s19_q), .in20(s20_q), .in21(s21_q),
    .in22(s22_q), .in23(s23_q), .in24(s24_q), .in25(s25_q), .in26(s26_q), .in27(s27_q), .in28(s28_q),
    .in29(s29_q), .in30(s30_q), .in31(s31_q), .out(LD2), .sel(LR2));
endmodule
