// Logisim project t3.circ as structural Verilog: 11 circuits, main circuit main
module main (
);

  wire ALUSRC, and_1_out, BNE, BRANCH, CLOCK, EXCOUT, JR, JUMP, LINK, MEMREAD, MEMTOREG, MEMWRITE, MTC0,
       multiplexer_5_out, not_1_out, or_1_out, OVERF, RegDST, WRITE_REG, WRITEREGEX, ZERO;
  wire [1:0] ALUOP;
  wire [3:0] OP;
  wire [4:0] multiplexer_8_out, multiplexer_9_out, RD, RS, RT, SHAMT, WR, WR_EXCEPCT;
  wire [5:0] FUNCT, OPCODE;
  wire [15:0] IMM;
  wire [25:0] ADDR;
  wire [31:0] adder_1_out, EPC, IMM32, LD1, \memã³ria_de_dados_1_out_6 ,
       \memã³ria_de_instruã_ãµes_1_instruã_ã_o , MFC0R, multiplexer_1_out, multiplexer_2_out,
       multiplexer_3_out, multiplexer_4_out, multiplexer_6_out, multiplexer_7_out, multiplexer_11_out,
       multiplexer_12_out, multiplexer_13_out, multiplexer_14_out, n2_conc_1_out_3, PC_4, PC_q,
       registradores_1_ld2, RESULT;

  Clock clock_1 (.out(CLOCK));
  Multiplexer #(.width(32), .enable("false")) multiplexer_1 (
    .in0(multiplexer_7_out), .in1(LD1), .out(multiplexer_1_out), .sel(JR));
  Multiplexer #(.width(32), .enable("false")) multiplexer_2 (
    .in0(multiplexer_1_out), .in1(n2_conc_1_out_3), .out(multiplexer_2_out), .sel(JUMP));
  Multiplexer #(.width(32), .enable("false")) multiplexer_3 (
    .in0(RESULT), .in1(LD1), .out(multiplexer_3_out), .sel(MTC0));
  not not_1 (not_1_out, ZERO);
  Multiplexer #(.width(32), .enable("false")) multiplexer_4 (
    .in0(multiplexer_2_out), .in1(32'h800000), .out(multiplexer_4_out), .sel(OVERF));
  Multiplexer #(.enable("false")) multiplexer_5 (.in0(ZERO), .in1(not_1_out), .out(multiplexer_5_out), .sel(BNE));
  Multiplexer #(.width(32), .enable("false")) multiplexer_6 (
    .in0(multiplexer_4_out), .in1(EPC), .out(multiplexer_6_out), .sel(EXCOUT));
  Multiplexer #(.width(32), .enable("false")) multiplexer_7 (
    .in0(PC_4), .in1(adder_1_out), .out(multiplexer_7_out), .sel(and_1_out));
  and and_1 (and_1_out, multiplexer_5_out, BRANCH);
  _2_conc u_2_conc_1 (.PC_4(PC_4), .ADDR(ADDR), .out_3(n2_conc_1_out_3));
  \Unidade_de_controle_de_exceÃ_Ãµes  \unidade_de_controle_de_exceã_ãµes_1  (
    .EXCEPT(OVERF), .EPCIN(PC_4), .WRIN(WR), .RESDATA(multiplexer_3_out), .WIRTERES(MTC0), .EPCOUT(EPC),
    .WROUT(WR_EXCEPCT), .MFC0OUT(MFC0R), .CLOCK(CLOCK));
  Register #(.width(32)) PC (.D(multiplexer_6_out), .Q(PC_q), .clk(CLOCK));  // open: en, clr
  Adder #(.width(32)) adder_1 (.a({IMM32[29:0], 2'b00}), .b(PC_4), .out(adder_1_out));  // open: cin, cout
  \MemÃ³ria_de_instruÃ_Ãµes  \memã³ria_de_instruã_ãµes_1  (
    .\EndereÃ_o (PC_q), .\InstruÃ_Ã_o (\memã³ria_de_instruã_ãµes_1_instruã_ã_o ));
  Adder #(.width(32)) adder_2 (.a(PC_q), .b(32'h4), .out(PC_4));  // open: cin, cout
  Decodificador decodificador_1 (
    .instrucao(\memã³ria_de_instruã_ãµes_1_instruã_ã_o ), .opcode(OPCODE), .funct(FUNCT), .shamt(SHAMT),
    .rd(RD), .rt(RT), .rs(RS), .imm(IMM), .addr(ADDR));
  Unidade_de_controle_principal unidade_de_controle_principal_1 (
    .in_1(OPCODE), .AluOp(ALUOP), .RegDST(RegDST), .WRITEREG(WRITE_REG), .ALUSRC(ALUSRC),
    .MemToReg(MEMTOREG), .MEMREAD(MEMREAD), .MEMWRITE(MEMWRITE), .BRANCH(BRANCH), .BNE(BNE), .JUMP(JUMP),
    .LINK(LINK), .MTC0(MTC0), .EXCOUT(EXCOUT), .WRITEREGEX(WRITEREGEX));
  Extersor_de_sinal extersor_de_sinal_1 (.in_1(IMM), .out_2(IMM32));
  Multiplexer #(.width(5), .enable("false")) multiplexer_8 (.in0(RT), .in1(RD), .out(multiplexer_8_out), .sel(RegDST));
  Multiplexer #(.width(5), .enable("false")) multiplexer_9 (
    .in0(multiplexer_8_out), .in1(WR_EXCEPCT), .out(multiplexer_9_out), .sel(EXCOUT));
  Multiplexer #(.width(5), .enable("false")) multiplexer_10 (
    .in0(multiplexer_9_out), .in1({5{1'b1}}), .out(WR), .sel(LINK));
  Multiplexer #(.width(32), .enable("false")) multiplexer_11 (
    .in0(multiplexer_14_out), .in1(MFC0R), .out(multiplexer_11_out), .sel(or_1_out));
  or or_1 (or_1_out, EXCOUT, WRITEREGEX);
  Multiplexer #(.width(32), .enable("false")) multiplexer_12 (
    .in0(multiplexer_11_out), .in1(PC_4), .out(multiplexer_12_out), .sel(LINK));
  Unidade_de_controle_ULA unidade_de_controle_ula_1 (.FUNCT(FUNCT), .ALUOP(ALUOP), .OP(OP), .JR(JR));
  Registradores registradores_1 (
    .LR1(RS), .LR2(RT), .WD(multiplexer_12_out), .WR(WR), .RW(WRITE_REG), .LD1(LD1),
    .LD2(registradores_1_ld2), .CLOCK(CLOCK));
  Multiplexer #(.width(32), .enable("false")) multiplexer_13 (
    .in0(registradores_1_ld2), .in1(IMM32), .out(multiplexer_13_out), .sel(ALUSRC));
  ULA ula_1 (
    .Resultado(RESULT), .ZERO(ZERO), .OVERFLOW(OVERF), .A(LD1), .B(multiplexer_13_out), .Operador(OP),
    .SHAMT(SHAMT));
  \MemÃ³ria_de_dados  \memã³ria_de_dados_1  (
    .EL(RESULT), .WD(registradores_1_ld2), .out_6(\memã³ria_de_dados_1_out_6 ), .Mem_Write(MEMWRITE),
    .Mem_Read(MEMREAD), .CLOCK(CLOCK));
  Multiplexer #(.width(32), .enable("false")) multiplexer_14 (
    .in0(RESULT), .in1(\memã³ria_de_dados_1_out_6 ), .out(multiplexer_14_out), .sel(MEMTOREG));

  // Notes on the sheet:
  //   A
  //   B
endmodule

module Unidade_de_controle_principal (
  input  [5:0] in_1,
  output [1:0] AluOp,
  output RegDST,
  output WRITEREG,
  output ALUSRC,
  output MemToReg,
  output MEMREAD,
  output MEMWRITE,
  output BRANCH,
  output BNE,
  output JUMP,
  output LINK,
  output MTC0,
  output EXCOUT,
  output WRITEREGEX
);

  wire ADDI, BEQ, J, JR, MFC0, or_5_out, R;
  wire [1:0] multiplexer_1_out;

  or or_1 (WRITEREG, LINK, R, MEMREAD, ADDI, EXCOUT, MFC0);
  or or_2 (ALUSRC, ADDI, MEMREAD, MEMWRITE);
  and u_R (R, ~in_1[0], ~in_1[1], ~in_1[2], ~in_1[3], ~in_1[4], ~in_1[5]);  // AND_Gate
  and u_J (J, ~in_1[0], in_1[1], ~in_1[2], ~in_1[3], ~in_1[4], ~in_1[5]);  // AND_Gate
  and JAL (LINK, in_1[0], in_1[1], ~in_1[2], ~in_1[3], ~in_1[4], ~in_1[5]);  // AND_Gate
  and u_JR (JR, ~in_1[0], ~in_1[1], ~in_1[2], ~in_1[3], ~in_1[4], ~in_1[5]);  // AND_Gate
  and u_mfc0 (MFC0, ~in_1[0], ~in_1[1], in_1[2], ~in_1[3], ~in_1[4], in_1[5]);  // AND_Gate
  and u_BNE (BNE, in_1[0], ~in_1[1], in_1[2], ~in_1[3], ~in_1[4], ~in_1[5]);  // AND_Gate
  or or_3 (BRANCH, BNE, BEQ);
  or or_4 (JUMP, J, LINK);
  and and_1 (RegDST, R, ~or_5_out);  // AND_Gate
  or or_5 (or_5_out, MEMREAD, MEMWRITE, ADDI, MFC0);
  and u_MTC0 (MTC0, in_1[0], ~in_1[1], ~in_1[2], ~in_1[3], ~in_1[4], in_1[5]);  // AND_Gate
  and RFE (EXCOUT, ~in_1[0], in_1[1], ~in_1[2], ~in_1[3], ~in_1[4], in_1[5]);  // AND_Gate
  and u_ADDI (ADDI, ~in_1[0], ~in_1[1], ~in_1[2], in_1[3], ~in_1[4], ~in_1[5]);  // AND_Gate
  and SW (MEMWRITE, in_1[0], in_1[1], ~in_1[2], in_1[3], ~in_1[4], in_1[5]);  // AND_Gate
  and LW (MEMREAD, in_1[0], in_1[1], ~in_1[2], ~in_1[3], ~in_1[4], in_1[5]);  // AND_Gate
  and u_BEQ (BEQ, ~in_1[0], ~in_1[1], in_1[2], ~in_1[3], ~in_1[4], ~in_1[5]);  // AND_Gate
  Multiplexer #(.width(2), .enable("false")) multiplexer_1 (
    .in0(2'b01), .in1(2'b10), .out(multiplexer_1_out), .sel(BRANCH));
  or or_6 (WRITEREGEX, EXCOUT, MFC0);
  Multiplexer #(.width(2), .enable("false")) multiplexer_2 (.in0(multiplexer_1_out), .in1(2'b00), .out(AluOp), .sel(R));

  assign MemToReg = MEMREAD;

  // Other names for the same wires on the sheet: JAL = LINK; LW = MEMREAD; OPCODE[5:0] = in_1; RFE = EXCOUT;
  //   SW = MEMWRITE

  // Notes on the sheet:
  //   R   000000
  //   J 000010
  //   JAL 000011
  //   ADDI 001000
  //   SW 101011
  //   LW 100011
  //   BEQ 000100
  //   BNE 000101
  //   MTC0 100001
  //   RFE 100010
  //   MFC0 100100
  //   EXCOUT 100000
  //   rt
  //   rt
  //   rt
endmodule

// REGISTRADORES
module Registradores (
  input  [4:0] LR1,
  input  [4:0] LR2,
  input  [31:0] WD,
  input  [4:0] WR,
  input  CLOCK,
  input  RW,
  output [31:0] LD1,
  output [31:0] LD2
);

  wire demultiplexer_2_out0, demultiplexer_2_out1, demultiplexer_2_out2, demultiplexer_2_out3,
       demultiplexer_2_out4, demultiplexer_2_out5, demultiplexer_2_out6, demultiplexer_2_out7,
       demultiplexer_2_out8, demultiplexer_2_out9, demultiplexer_2_out10, demultiplexer_2_out11,
       demultiplexer_2_out12, demultiplexer_2_out13, demultiplexer_2_out14, demultiplexer_2_out15,
       demultiplexer_2_out16, demultiplexer_2_out17, demultiplexer_2_out18, demultiplexer_2_out19,
       demultiplexer_2_out20, demultiplexer_2_out21, demultiplexer_2_out22, demultiplexer_2_out23,
       demultiplexer_2_out24, demultiplexer_2_out25, demultiplexer_2_out26, demultiplexer_2_out27,
       demultiplexer_2_out28, demultiplexer_2_out29, demultiplexer_2_out30, demultiplexer_2_out31;
  wire [31:0] _0_q, a0_q, a1_q, a2_q, a3_q, at_q, demultiplexer_1_out0, demultiplexer_1_out1,
       demultiplexer_1_out2, demultiplexer_1_out3, demultiplexer_1_out4, demultiplexer_1_out5,
       demultiplexer_1_out6, demultiplexer_1_out7, demultiplexer_1_out8, demultiplexer_1_out9,
       demultiplexer_1_out10, demultiplexer_1_out11, demultiplexer_1_out12, demultiplexer_1_out13,
       demultiplexer_1_out14, demultiplexer_1_out15, demultiplexer_1_out16, demultiplexer_1_out17,
       demultiplexer_1_out18, demultiplexer_1_out19, demultiplexer_1_out20, demultiplexer_1_out21,
       demultiplexer_1_out22, demultiplexer_1_out23, demultiplexer_1_out24, demultiplexer_1_out25,
       demultiplexer_1_out26, demultiplexer_1_out27, demultiplexer_1_out28, demultiplexer_1_out29,
       demultiplexer_1_out30, demultiplexer_1_out31, gp_q, k0_q, k1_q, ra_q, s0_q, s1_q, s2_q, s3_q, s4_q,
       s5_q, s6_q, s7_q, s8__fp_q, sp_q, t0_q, t1_q, t2_q, t3_q, t4_q, t5_q, t6_q, t7_q, t8_q, t9_q, v0_q,
       v1_q;

  Demultiplexer #(.select(5), .width(32), .enable("false")) demultiplexer_1 (
    .out0(demultiplexer_1_out0), .out1(demultiplexer_1_out1), .out2(demultiplexer_1_out2),
    .out3(demultiplexer_1_out3), .out4(demultiplexer_1_out4), .out5(demultiplexer_1_out5),
    .out6(demultiplexer_1_out6), .out7(demultiplexer_1_out7), .out8(demultiplexer_1_out8),
    .out9(demultiplexer_1_out9), .out10(demultiplexer_1_out10), .out11(demultiplexer_1_out11),
    .out12(demultiplexer_1_out12), .out13(demultiplexer_1_out13), .out14(demultiplexer_1_out14),
    .out15(demultiplexer_1_out15), .out16(demultiplexer_1_out16), .out17(demultiplexer_1_out17),
    .out18(demultiplexer_1_out18), .out19(demultiplexer_1_out19), .out20(demultiplexer_1_out20),
    .out21(demultiplexer_1_out21), .out22(demultiplexer_1_out22), .out23(demultiplexer_1_out23),
    .out24(demultiplexer_1_out24), .out25(demultiplexer_1_out25), .out26(demultiplexer_1_out26),
    .out27(demultiplexer_1_out27), .out28(demultiplexer_1_out28), .out29(demultiplexer_1_out29),
    .out30(demultiplexer_1_out30), .out31(demultiplexer_1_out31), .in(WD), .sel(WR));
  Demultiplexer #(.select(5), .enable("false")) demultiplexer_2 (
    .out0(demultiplexer_2_out0), .out1(demultiplexer_2_out1), .out2(demultiplexer_2_out2),
    .out3(demultiplexer_2_out3), .out4(demultiplexer_2_out4), .out5(demultiplexer_2_out5),
    .out6(demultiplexer_2_out6), .out7(demultiplexer_2_out7), .out8(demultiplexer_2_out8),
    .out9(demultiplexer_2_out9), .out10(demultiplexer_2_out10), .out11(demultiplexer_2_out11),
    .out12(demultiplexer_2_out12), .out13(demultiplexer_2_out13), .out14(demultiplexer_2_out14),
    .out15(demultiplexer_2_out15), .out16(demultiplexer_2_out16), .out17(demultiplexer_2_out17),
    .out18(demultiplexer_2_out18), .out19(demultiplexer_2_out19), .out20(demultiplexer_2_out20),
    .out21(demultiplexer_2_out21), .out22(demultiplexer_2_out22), .out23(demultiplexer_2_out23),
    .out24(demultiplexer_2_out24), .out25(demultiplexer_2_out25), .out26(demultiplexer_2_out26),
    .out27(demultiplexer_2_out27), .out28(demultiplexer_2_out28), .out29(demultiplexer_2_out29),
    .out30(demultiplexer_2_out30), .out31(demultiplexer_2_out31), .in(RW), .sel(WR));
  Register #(.width(32)) _0 (.D({32{1'b0}}), .Q(_0_q), .clk(CLOCK));  // open: en, clr
  Register #(.width(32)) at (.D(demultiplexer_1_out1), .en(demultiplexer_2_out1), .Q(at_q), .clk(CLOCK));  // open: clr
  Register #(.width(32)) v0 (.D(demultiplexer_1_out2), .en(demultiplexer_2_out2), .Q(v0_q), .clk(CLOCK));  // open: clr
  Register #(.width(32)) v1 (.D(demultiplexer_1_out3), .en(demultiplexer_2_out3), .Q(v1_q), .clk(CLOCK));  // open: clr
  Register #(.width(32)) a0 (.D(demultiplexer_1_out4), .en(demultiplexer_2_out4), .Q(a0_q), .clk(CLOCK));  // open: clr
  Register #(.width(32)) a1 (.D(demultiplexer_1_out5), .en(demultiplexer_2_out5), .Q(a1_q), .clk(CLOCK));  // open: clr
  Register #(.width(32)) a2 (.D(demultiplexer_1_out6), .en(demultiplexer_2_out6), .Q(a2_q), .clk(CLOCK));  // open: clr
  Register #(.width(32)) a3 (.D(demultiplexer_1_out7), .en(demultiplexer_2_out7), .Q(a3_q), .clk(CLOCK));  // open: clr
  Register #(.width(32)) t0 (.D(demultiplexer_1_out8), .en(demultiplexer_2_out8), .Q(t0_q), .clk(CLOCK));  // open: clr
  Register #(.width(32)) t1 (.D(demultiplexer_1_out9), .en(demultiplexer_2_out9), .Q(t1_q), .clk(CLOCK));  // open: clr
  Register #(.width(32)) t2 (
    .D(demultiplexer_1_out10), .en(demultiplexer_2_out10), .Q(t2_q), .clk(CLOCK));  // open: clr
  Register #(.width(32)) t3 (.D(demultiplexer_1_out11), .en(demultiplexer_2_out11), .Q(t3_q));  // open: clk, clr
  Register #(.width(32)) t4 (
    .D(demultiplexer_1_out12), .en(demultiplexer_2_out12), .Q(t4_q), .clk(CLOCK));  // open: clr
  Register #(.width(32)) t5 (
    .D(demultiplexer_1_out13), .en(demultiplexer_2_out13), .Q(t5_q), .clk(CLOCK));  // open: clr
  Register #(.width(32)) t6 (
    .D(demultiplexer_1_out14), .en(demultiplexer_2_out14), .Q(t6_q), .clk(CLOCK));  // open: clr
  Register #(.width(32)) t7 (
    .D(demultiplexer_1_out15), .en(demultiplexer_2_out15), .Q(t7_q), .clk(CLOCK));  // open: clr
  Register #(.width(32)) s0 (
    .D(demultiplexer_1_out16), .en(demultiplexer_2_out16), .Q(s0_q), .clk(CLOCK));  // open: clr
  Register #(.width(32)) s1 (
    .D(demultiplexer_1_out17), .en(demultiplexer_2_out17), .Q(s1_q), .clk(CLOCK));  // open: clr
  Register #(.width(32)) s2 (
    .D(demultiplexer_1_out18), .en(demultiplexer_2_out18), .Q(s2_q), .clk(CLOCK));  // open: clr
  Register #(.width(32)) s3 (
    .D(demultiplexer_1_out19), .en(demultiplexer_2_out19), .Q(s3_q), .clk(CLOCK));  // open: clr
  Register #(.width(32)) s4 (
    .D(demultiplexer_1_out20), .en(demultiplexer_2_out20), .Q(s4_q), .clk(CLOCK));  // open: clr
  Register #(.width(32)) s5 (
    .D(demultiplexer_1_out21), .en(demultiplexer_2_out21), .Q(s5_q), .clk(CLOCK));  // open: clr
  Register #(.width(32)) s6 (
    .D(demultiplexer_1_out22), .en(demultiplexer_2_out22), .Q(s6_q), .clk(CLOCK));  // open: clr
  Register #(.width(32)) s7 (
    .D(demultiplexer_1_out23), .en(demultiplexer_2_out23), .Q(s7_q), .clk(CLOCK));  // open: clr
  Register #(.width(32)) t8 (
    .D(demultiplexer_1_out24), .en(demultiplexer_2_out24), .Q(t8_q), .clk(CLOCK));  // open: clr
  Register #(.width(32)) t9 (
    .D(demultiplexer_1_out25), .en(demultiplexer_2_out25), .Q(t9_q), .clk(CLOCK));  // open: clr
  Register #(.width(32)) k0 (
    .D(demultiplexer_1_out26), .en(demultiplexer_2_out26), .Q(k0_q), .clk(CLOCK));  // open: clr
  Register #(.width(32)) k1 (.D(demultiplexer_1_out27), .en(demultiplexer_2_out27), .Q(k1_q));  // open: clk, clr
  Register #(.width(32)) gp (
    .D(demultiplexer_1_out28), .en(demultiplexer_2_out28), .Q(gp_q), .clk(CLOCK));  // open: clr
  Register #(.width(32)) sp (
    .D(demultiplexer_1_out29), .en(demultiplexer_2_out29), .Q(sp_q), .clk(CLOCK));  // open: clr
  Register #(.width(32)) s8__fp (
    .D(demultiplexer_1_out30), .en(demultiplexer_2_out30), .Q(s8__fp_q), .clk(CLOCK));  // open: clr
  Register #(.width(32)) ra (
    .D(demultiplexer_1_out31), .en(demultiplexer_2_out31), .Q(ra_q), .clk(CLOCK));  // open: clr
  Multiplexer #(.select(5), .width(32), .enable("false")) multiplexer_1 (
    .in0(_0_q), .in1(at_q), .in2(v0_q), .in3(v1_q), .in4(a0_q), .in5(a1_q), .in6(a2_q), .in7(a3_q),
    .in8(t0_q), .in9(t1_q), .in10(t2_q), .in11(t3_q), .in12(t4_q), .in13(t5_q), .in14(t6_q), .in15(t7_q),
    .in16(s0_q), .in17(s1_q), .in18(s2_q), .in19(s3_q), .in20(s4_q), .in21(s5_q), .in22(s6_q), .in23(s7_q),
    .in24(t8_q), .in25(t9_q), .in26(k0_q), .in27(k1_q), .in28(gp_q), .in29(sp_q), .in30(s8__fp_q),
    .in31(ra_q), .out(LD1), .sel(LR1));
  Multiplexer #(.select(5), .width(32), .enable("false")) multiplexer_2 (
    .in0(_0_q), .in1(at_q), .in2(v0_q), .in3(v1_q), .in4(a0_q), .in5(a1_q), .in6(a2_q), .in7(a3_q),
    .in8(t0_q), .in9(t1_q), .in10(t2_q), .in11(t3_q), .in12(t4_q), .in13(t5_q), .in14(t6_q), .in15(t7_q),
    .in16(s0_q), .in17(s1_q), .in18(s2_q), .in19(s3_q), .in20(s4_q), .in21(s5_q), .in22(s6_q), .in23(s7_q),
    .in24(t8_q), .in25(t9_q), .in26(k0_q), .in27(k1_q), .in28(gp_q), .in29(sp_q), .in30(s8__fp_q),
    .in31(ra_q), .out(LD2), .sel(LR2));
endmodule

module ULA (
  input  [3:0] Operador,
  input  [4:0] SHAMT,
  input  [31:0] A,
  input  [31:0] B,
  output [31:0] Resultado,
  output ZERO,
  output OVERFLOW
);

  wire and_2_out, and_3_out, and_4_out, and_5_out, comparator_2_eq, comparator_3_eq, not_1_out, not_2_out,
       not_3_out, not_4_out, not_5_out, not_6_out;
  wire [0:0] comparator_1_lt;
  wire [31:0] adder_1_out, and_1_out, nor_1_out, or_1_out, shifter_1_out, shifter_2_out, subtractor_1_out,
       xor_1_out;

  assign and_1_out = A & B;  // AND_Gate and_1, 32 bits wide
  assign or_1_out = A | B;  // OR_Gate or_1, 32 bits wide
  assign nor_1_out = ~(A | B);  // NOR_Gate nor_1, 32 bits wide
  assign xor_1_out = A ^ B;  // XOR_Gate xor_1, 32 bits wide
  Adder #(.width(32)) adder_1 (.a(A), .b(B), .out(adder_1_out));  // open: cin, cout
  Subtractor #(.width(32)) subtractor_1 (.a(A), .b(B), .out(subtractor_1_out));  // open: bin, bout
  Shifter #(.width(32)) shifter_1 (.in(A), .\dist (SHAMT), .out(shifter_1_out));
  Shifter #(.width(32), .shift("lr")) shifter_2 (.in(A), .\dist (SHAMT), .out(shifter_2_out));
  Comparator #(.width(32)) comparator_1 (.a(A), .b(B), .lt(comparator_1_lt[0]));  // open: gt, eq
  Comparator #(.width(4)) comparator_2 (.a(Operador), .b(4'b0100), .eq(comparator_2_eq));  // open: gt, lt
  Comparator #(.width(4)) comparator_3 (.a(Operador), .b(4'b0101), .eq(comparator_3_eq));  // open: gt, lt
  not not_1 (not_1_out, Resultado[31]);
  and and_2 (and_2_out, not_1_out, comparator_2_eq, B[31], A[31]);
  and and_3 (and_3_out, Resultado[31], comparator_2_eq, not_2_out, not_3_out);
  not not_2 (not_2_out, B[31]);
  not not_3 (not_3_out, A[31]);
  and and_4 (and_4_out, Resultado[31], comparator_3_eq, B[31], not_4_out);
  not not_4 (not_4_out, A[31]);
  not not_5 (not_5_out, Resultado[31]);
  and and_5 (and_5_out, not_5_out, comparator_3_eq, not_6_out, A[31]);
  not not_6 (not_6_out, B[31]);
  Multiplexer #(.select(4), .width(32), .enable("false")) multiplexer_1 (
    .in0(and_1_out), .in1(or_1_out), .in2(nor_1_out), .in3(xor_1_out), .in4(adder_1_out),
    .in5(subtractor_1_out), .in6(shifter_1_out), .in7(shifter_2_out), .in8({{31{1'b0}}, comparator_1_lt[0]}),
    .out(Resultado), .sel(Operador));  // open: in9, in10, in11, in12, in13, in14, in15
  Comparator #(.width(32)) comparator_4 (.a(Resultado), .b({32{1'b0}}), .eq(ZERO));  // open: gt, lt
  or or_2 (OVERFLOW, and_2_out, and_3_out, and_4_out, and_5_out);

  // Notes on the sheet:
  //   Shift Amount
  //   negativo + negativo = positivo
  //   positivo + positivo = negativo
  //   positivo - negativo = negativo
  //   negativo - positivo = positivo
endmodule

// DECODIFIER
module Decodificador (
  input  [31:0] instrucao,
  output [5:0] opcode,
  output [5:0] funct,
  output [4:0] shamt,
  output [4:0] rd,
  output [4:0] rt,
  output [4:0] rs,
  output [15:0] imm,
  output [25:0] addr
);

  wire I_out, J_out, Jal_out, or_1_out, R_out;
  wire [25:0] \NÃ_o_R ;
  wire [25:16] demultiplexer_1_out1, demultiplexer_2_out0;

  and J (J_out, ~instrucao[31], ~instrucao[30], ~instrucao[29], ~instrucao[28], instrucao[27], ~instrucao[26]);  // AND_Gate
  Demultiplexer #(.width(26), .enable("false")) demultiplexer_1 (
    .out0(\NÃ_o_R ), .out1({demultiplexer_1_out1, rd, shamt, funct}), .in(instrucao[25:0]), .sel(R_out));
  and R (R_out, ~instrucao[31], ~instrucao[30], ~instrucao[29], ~instrucao[28], ~instrucao[27], ~instrucao[26]);  // AND_Gate
  or or_1 (or_1_out, J_out, Jal_out);
  and Jal (Jal_out, ~instrucao[31], ~instrucao[30], ~instrucao[29], ~instrucao[28], instrucao[27], instrucao[26]);  // AND_Gate
  and I (I_out, ~R_out, ~or_1_out);  // AND_Gate
  Demultiplexer #(.width(26), .enable("false")) demultiplexer_2 (
    .out0({demultiplexer_2_out0, imm}), .out1(addr), .in(\NÃ_o_R ), .sel(or_1_out));
  Multiplexer #(.width(5), .enable("false")) multiplexer_1 (
    .in0(demultiplexer_1_out1[20:16]), .in1(demultiplexer_2_out0[20:16]), .out(rt), .sel(I_out));
  Multiplexer #(.width(5), .enable("false")) multiplexer_2 (
    .in0(demultiplexer_1_out1[25:21]), .in1(demultiplexer_2_out0[25:21]), .out(rs), .sel(I_out));

  assign opcode = instrucao[31:26];
endmodule

module Unidade_de_controle_ULA (
  input  [5:0] FUNCT,
  input  [1:0] ALUOP,
  output [3:0] OP,
  output JR
);

  wire [3:0] multiplexer_1_out;
  wire [5:0] and_2_out;
  wire [5:4] not_1_out;
  wire [5:5] and_1_out;

  Multiplexer #(.select(2), .width(4), .enable("false")) multiplexer_1 (
    .in0(FUNCT[5:2]), .in1(4'b0100), .in2(4'b0101), .out(multiplexer_1_out), .sel(ALUOP));  // open: in3
  not not_1 (not_1_out[4], ALUOP[0]);
  not not_2 (not_1_out[5], ALUOP[1]);
  and and_1 (and_1_out[5], ~FUNCT[0], ~FUNCT[1], ~FUNCT[2], ~FUNCT[3], FUNCT[4], FUNCT[5]);  // AND_Gate
  assign and_2_out = {6{and_1_out[5]}} & {not_1_out, 4'b0000};  // AND_Gate and_2, 6 bits wide
  and and_3 (JR, and_2_out[4], and_2_out[5]);
  Multiplexer #(.width(4), .enable("false")) multiplexer_2 (.in0(multiplexer_1_out), .in1(4'b0100), .out(OP), .sel(JR));

  // Notes on the sheet:
  //   000000 AND
  //   000100 OR
  //   001000 NOR
  //   001100 XOR
  //   010000 ADD
  //   010100 SUB
  //   011000 SLL
  //   011100 SLR
  //   100000 SLT
  //   110000 JR
endmodule

// DATA MEM
module \MemÃ³ria_de_dados  (
  input  CLOCK,
  input  Mem_Write,
  input  Mem_Read,
  input  [31:0] EL,
  input  [31:0] WD,
  output [31:0] out_6
);

  RAM #(.addrWidth(24), .dataWidth(32), .bus("separate")) ram_1 (
    .addr(EL[23:0]), .din(WD), .data(out_6), .str(Mem_Write), .clk(CLOCK), .ld(Mem_Read));  // open: sel, clr
endmodule

// INST MEM
module \MemÃ³ria_de_instruÃ_Ãµes  (
  input  [31:0] \EndereÃ_o ,
  output [31:0] \InstruÃ_Ã_o 
);

  ROM #(.addrWidth(24), .dataWidth(32)) rom_1 (.addr(\EndereÃ_o [25:2]), .data(\InstruÃ_Ã_o ));  // open: sel

  // Notes on the sheet:
  //   contents of rom_1 (hex, n*v repeats v):
  //   2084810 2097151*0 901a0000 d010 841a0000 88000000 6291552*0 123123 287*0 87400000
endmodule

// SIGN EXTENDED
module Extersor_de_sinal (
  input  [15:0] in_1,
  output [31:0] out_2
);


  assign out_2 = {{17{in_1[15]}}, in_1[14:0]};
endmodule

module \Unidade_de_controle_de_exceÃ_Ãµes  (
  input  EXCEPT,
  input  [31:0] EPCIN,
  input  [4:0] WRIN,
  input  [31:0] RESDATA,
  input  CLOCK,
  input  WIRTERES,
  output [31:0] EPCOUT,
  output [4:0] WROUT,
  output [31:0] MFC0OUT
);

  wire or_1_out;

  or or_1 (or_1_out, EXCEPT, WIRTERES);
  Register #(.width(32)) EPC (.D(EPCIN), .en(EXCEPT), .Q(EPCOUT), .clk(CLOCK));  // open: clr
  Register #(.width(5)) WR (.D(WRIN), .en(EXCEPT), .Q(WROUT), .clk(CLOCK));  // open: clr
  Register #(.width(32)) RES (.D(RESDATA), .en(or_1_out), .Q(MFC0OUT), .clk(CLOCK));  // open: clr
endmodule

module _2_conc (
  input  [31:0] PC_4,
  input  [25:0] ADDR,
  output [31:0] out_3
);

  Shifter #(.width(28)) shifter_1 (.in({2'b00, ADDR}), .\dist (5'b00010), .out(out_3[27:0]));

  assign out_3[31:28] = PC_4[31:28];
endmodule
